# Fritzing sketch MIDTERM-PROJECT (saved by Fritzing 0.8.7b)
breadboards: 1

parts:
  R1 = Resistor [tolerance=±10% resistance=1.1k package=THT]
  R2 = Resistor [tolerance=±5% resistance=1.5k package=THT]
  R3 = Resistor [tolerance=±5% resistance=2k package=THT]
  R4 = Resistor [tolerance=±5% resistance=1.8k package=THT]
  Part2 = Arduino Mega ADK (Rev3)

nets:
  N1: R1.Pin_1, R2.Pin_0, Part2.A0
  N2: R2.Pin_1, R3.Pin_0, Part2.A1
  N3: R3.Pin_1, R4.Pin_0, Part2.A2
  N4: R4.Pin_1, Part2.5V
